// Digital circuit Hazard-Unit.dig as structural Verilog
module Hazard_Unit (
  input  [4:0] RR0,
  input  [4:0] RR1,
  input  [4:0] WR_4,
  input  RFW_4,
  input  [4:0] WR_3,
  input  RFW_3,
  input  MLD_3,
  input  EN,
  input  CLR,
  input  PCbr_2,
  output [1:0] FRD0,
  output [1:0] FRD1,
  output CLR_IF_EX,
  output CLR_EX_DR,
  output EN_PC,
  output EN_IF_DR,
  output EN_DR_EX,
  output CLR_EX_MEM
);

  wire and_1_out, and_2_out, and_3_out, and_4_out, and_5_out, comparator_1_eq, comparator_2_eq,
       comparator_3_eq, comparator_4_eq, comparator_5_eq, comparator_6_eq, or_1_out, sel;

  Comparator #(.Bits(5)) comparator_1 (.a(RR0), .b(WR_4), .eq(comparator_1_eq));  // open: gt, lt
  Comparator #(.Bits(5)) comparator_2 (.a(RR0), .b(WR_3), .eq(comparator_2_eq));  // open: gt, lt
  Comparator #(.Bits(5)) comparator_3 (.a(RR1), .b(WR_4), .eq(comparator_3_eq));  // open: gt, lt
  Comparator #(.Bits(5)) comparator_4 (.a(RR1), .b(WR_3), .eq(comparator_4_eq));  // open: gt, lt
  Comparator #(.Bits(5)) comparator_5 (.a(RR0), .b(WR_3), .eq(comparator_5_eq));  // open: gt, lt
  Comparator #(.Bits(5)) comparator_6 (.a(RR1), .b(WR_3), .eq(comparator_6_eq));  // open: gt, lt
  and and_1 (and_1_out, MLD_3, RFW_3);
  Multiplexer multiplexer_1 (.sel(PCbr_2), .in_0(CLR), .in_1(1'b1), .out(CLR_IF_EX));
  and and_2 (and_2_out, comparator_1_eq, RFW_4);
  and and_3 (and_3_out, comparator_2_eq, RFW_3);
  and and_4 (and_4_out, comparator_3_eq, RFW_4);
  and and_5 (and_5_out, comparator_4_eq, RFW_3);
  or or_1 (or_1_out, comparator_5_eq, comparator_6_eq);
  PriorityEncoder #(.Selector_Bits(2)) priorityencoder_1 (
    .in0(1'b1), .in1(and_2_out), .in2(and_3_out), .in3(1'b0), .num(FRD0));  // open: any
  PriorityEncoder #(.Selector_Bits(2)) priorityencoder_2 (
    .in0(1'b1), .in1(and_4_out), .in2(and_5_out), .in3(1'b0), .num(FRD1));  // open: any
  and and_6 (sel, or_1_out, and_1_out);
  Multiplexer multiplexer_2 (.sel(PCbr_2), .in_0(CLR), .in_1(1'b1), .out(CLR_EX_DR));
  Multiplexer multiplexer_3 (.sel(sel), .in_0(EN), .in_1(1'b0), .out(EN_PC));
  Multiplexer multiplexer_4 (.sel(sel), .in_0(1'b1), .in_1(1'b0), .out(EN_IF_DR));
  Multiplexer multiplexer_5 (.sel(sel), .in_0(1'b1), .in_1(1'b0), .out(EN_DR_EX));
  Multiplexer multiplexer_6 (.sel(sel), .in_0(CLR), .in_1(1'b1), .out(CLR_EX_MEM));

  // Other names for the same wires on the sheet: RR0_2[4:0] = RR0; RR1_2[4:0] = RR1
endmodule
